# Fritzing sketch Untitled Sketch 7 (saved by Fritzing 0.9.3b)

parts:
  DS1 = DS18B20 1-Wire Temperature Sensor Probe Cable
  M1 = MAX30102
  U1 = NodeMCU V3.0
  Part1 = Arduino Nano (Rev3.0)
  Part2 = LCD1602-I2C
  R1 = Resistor [tolerance=±5% resistance=220 package=THT]
  DHT1 = DHT11 Humitidy and Temperature Sensor
  Power_plug2 = Power plug
  R2 = Resistor [tolerance=±5% resistance=220 package=THT]  # not connected
  R3 = Resistor [tolerance=±5% resistance=220 package=THT]  # not connected

nets:
  GND: DS1.GND, DS1.shield, DHT1.GND
  N1: DS1.DQ, U1.D5, R1.Pin_0
  VDD: DS1.VDD, U1.VU, Part2.VCC, R1.Pin_1, DHT1.VDD
  VIN: M1.VIN, Part1.5V
  N2: M1.SCL, Part1.A5
  N3: M1.SDA, Part1.A4
  GND_2: M1.GND, U1.GND, Part1.GND, Part2.GND, Power_plug2.GND
  N4: U1.D1, Part2.SDA
  N5: U1.D2, Part2.SCL
  N6: U1.D6, Part1.D2
  N7: U1.D7, Part1.D3
  N8: U1.D8, DHT1.DATA
  VIN_2: U1.Vin, Part1.VIN, Power_plug2.VCC

notes:
  5Vdc power

custom parts:
  MAX30102: Oximeter module using the MAX30102 chip. You may wish to read (and check your module) this post on power problems with these modules: https://reedpaper.wordpress.com/2018/08/22/pulse-oximeter-max30100-max30102-how-to-fix-wrong-board/ . As usual, if you want the mounting holes in pcb, you need to drag a hole over the pad in silkscreen to actually drill the hole (by default they are not drilled)
  NodeMCU V3.0: ESP8266 based NodeMCU
  LCD1602-I2C: A standard character display, usually with 2x16 characters. Comes in many colors with LCM1602 IIC attached.
  DHT11 Humitidy and Temperature Sensor: DHT11 Humidity and Temperature Sensor
