# Fritzing sketch Untitled Sketch (saved by Fritzing 0.9.3b)

parts:
  SIM800L_BO1 = SIM800L BO
  PIR1 = PIR sensor
  Part1 = Arduino Uno (Rev3)
  J1 = Piezo Speaker
  VCC1 = Battery block 9V
  U1 = LM2596 step down module
  o1 = Module display OLED I2C 128x64 SSD1306 [package=THT]

nets:
  N1: SIM800L_BO1.PIN2, U1.OUT+
  N2: SIM800L_BO1.pin_4, Part1.D10_PWM/SS
  N3: SIM800L_BO1.pin_5, Part1.D11_PWM/MOSI
  GND: SIM800L_BO1.pin_6, PIR1.GND, Part1.GND, J1.pin1, VCC1.-, U1.IN-, U1.OUT-, o1.GND
  VDD: PIR1.VDD, Part1.5V, o1.VCC
  N4: PIR1.SIG, Part1.D3_PWM
  N5: Part1.A4/SDA, o1.SDA
  N6: Part1.A5/SCL, o1.SCL
  N7: Part1.D12/MISO, J1.pin2
  N8: Part1.VIN, VCC1.+, U1.IN+

custom parts:
  LM2596 step down module: LM2596 DC-DC step down power supply module 3 A.
  Module display OLED I2C 128x64 SSD1306: Ecran OLED I2C SSD163 de 128x64 avec connexion I2C
