# Fritzing sketch Untitled Sketch (saved by Fritzing 0.9.3b)

parts:
  Part1 = RFID-RC522-v2
  U1 = NodeMCU V3.0
  Part2 = LCD1602-I2C
  SERVO1 = Tower Pro SG90 servo [part_number=101246]
  J1 = Piezo Speaker

nets:
  N1: Part1.SDA, U1.D3
  N2: Part1.SCK, U1.D5
  N3: Part1.MOSI, U1.D6
  N4: Part1.MISO, U1.D7
  N5: Part1.GND, U1.GND#13, U1.GND#16
  N6: Part1.RST, U1.D4
  3.3V: Part1.3.3V, U1.3V3
  N7: U1.D0, J1.pin2
  N8: U1.D1, Part2.SDA
  N9: U1.D2, Part2.SCL
  N10: U1.D8, SERVO1.Signal
  N11: U1.VU, Part2.VCC
  GND: U1.GND#41, Part2.GND, SERVO1.GND, J1.pin1

custom parts:
  RFID-RC522-v2: A simple China made RFID-RC522 Reader; do check the pin labels, as this is a MFRC522 based clone.
  NodeMCU V3.0: ESP8266 based NodeMCU
  LCD1602-I2C: A standard character display, usually with 2x16 characters. Comes in many colors with LCM1602 IIC attached.
  Tower Pro SG90 servo: Original file by John De Cristofaro http://www.adafruit.com/products/1449 Adafruit Feedback Servo (Small) Edited by: e-radionica.com 28/9/2015
