# Fritzing sketch robot (saved by Fritzing 0.9.3b)

parts:
  S1 = H-Bridge with L298N
  Part1 = Arduino Uno (Rev3)
  M1 = fc-51 [package=THT]
  M2 = fc-51 [package=THT]
  M3 = fc-51 [package=THT]
  M4 = DC Motor
  M5 = DC Motor
  M6 = DC Motor
  M7 = DC Motor
  M8 = DC Motor  # not connected
  Q2 = PNP-Transistor [package="TO92 [THT]"]
  R1 = Resistor [tolerance=±5% resistance=220 package=THT]
  R2 = Resistor [tolerance=±5% resistance=220 package=THT]
  U1 = SWITCH_SPDT [package=kps-1290]
  S2 = SPST Switch [package=switch-spdt_lock.007s]
  OMRON1 = OMRON PCB Power Relay – G5LE [part_number="G5LE-1\n" package=THT]
  S3 = SPST Switch [package=switch-spdt]
  OMRON2 = OMRON PCB Power Relay – G5LE [part_number="G5LE-1\n" package=THT]
  Q3 = PNP-Transistor [package="TO92 [THT]"]
  U2 = Voltage Regulator - 5V [package="DPak [SMD]"]
  C3 = Capacitor Polarized [package=cpol-radial-1000uf-25v]
  C4 = Capacitor Polarized [package=cpol-radial-1000uf-25v]
  R3 = Resistor [tolerance=±5% resistance=220 package="2010 [SMD]"]
  R4 = Resistor [tolerance=±5% resistance=220 package="2010 [SMD]"]
  U3 = SWITCH-SPST-2 [package=switch-spst-vertical]
  U4 = LIPO-1000mAh [package=lipo-1000]
  Part2 = SRF05 Ultrasonic Rangefinder

nets:
  N1: S1.12V, U2.input_voltage, C3.+, U3.O
  5V: S1.5V, Part1.VIN, R3.Pin_0, R4.Pin_0
  N2: S1.ENA, Part1.D11_PWM/MOSI
  N3: S1.IN1, Part1.D6_PWM
  N4: S1.IN2, Part1.D5_PWM
  N5: S1.IN3, Part1.D4
  N6: S1.IN4, Part1.D2
  N7: S1.ENB, Part1.D3_PWM
  N8: S1.M1-01, M6.pin_2, M7.pin_2
  N9: S1.M1-02, M6.pin_1, M7.pin_1
  N10: S1.M2-01, M4.pin_2, M5.pin_2
  N11: S1.M2-02, M4.pin_1, M5.pin_1
  N12: Part1.A0, M3.pin1
  N13: Part1.A1, M2.pin1
  N14: Part1.A2, M1.pin1
  N15: Part1.A3, R1.Pin_0
  N16: Part1.A4/SDA, R2.Pin_0
  N17: Part1.D8, Part2.Echo
  N18: Part1.D9_PWM, S2.S, R3.Pin_1
  N19: Part1.D10_PWM/SS, S3.S, R4.Pin_1
  N20: Part1.D12/MISO, U1.P
  N21: Part1.D7, Part2.Trig
  5V_2: Part1.5V, M1.pin3, M2.pin3, M3.pin3, Part2.VCC
  GND: Part1.GND, M1.pin2, M2.pin2, M3.pin2, Q2.E, Q3.C, Part2.GND
  N22: Q2.B, OMRON2.COIL2
  N23: Q2.C, R2.Pin_1
  N24: R1.Pin_1, Q3.B
  N25: S2.P, S3.P
  N26: OMRON1.COIL1, OMRON1.C, OMRON2.COIL1, OMRON2.C
  N27: OMRON1.COIL2, Q3.E
  N28: U2.GND, C3.-, C4.-
  N29: U2.output_voltage, C4.+
  N30: U3.P, U4.+

notes:
  3 Batteries in series

custom parts:
  H-Bridge with L298N: h-bridge
