# Fritzing sketch Untitled Sketch (saved by Fritzing 0.9.3b)

parts:
  Part1 = u-blox NEO-6M GPS Breakout
  U1 = NodeMCU V3.0
  Part2 = LCD1602-I2C
  S1 = Pushbutton [package="[SMD]"]
  S2 = Pushbutton [package="[SMD]"]
  R1 = Resistor [tolerance=±5% resistance=220 package="2512 [SMD]"]  # not connected
  R2 = Resistor [tolerance=±5% resistance=220 package=THT]  # not connected
  IC1 = Voltage Regulator [package=to220-igo]
  C1 = Capacitor Polarized [package=panasonic_d]
  C3 = Capacitor Polarized [package=panasonic_d]
  VCC1 = Battery block 9V

nets:
  GND: Part1.GND, U1.GND, Part2.GND, IC1.IN, C1.-, C3.-
  VCC: Part1.VCC, U1.Vin, Part2.VCC, IC1.OUT, C3.+
  N1: Part1.TXD, U1.D6
  N2: Part1.RXD, U1.D7
  N3: U1.D1, Part2.SDA
  N4: U1.D2, Part2.SCL
  N5: U1.D3, S1.Pin_1, S1.Pin_2
  N6: U1.D4, S2.Pin_3, S2.Pin_4
  N7: IC1.GND, C1.+, VCC1.+

notes:
  Power supply
  GPS Module
  Scan
  connectiviity test

custom parts:
  NodeMCU V3.0: ESP8266 based NodeMCU
  LCD1602-I2C: A standard character display, usually with 2x16 characters. Comes in many colors with LCM1602 IIC attached.
