# Fritzing sketch Untitled Sketch 2 (saved by Fritzing 0.9.3b)

parts:
  M1 = fc-51 [package=THT]
  M2 = fc-51 [package=THT]
  M3 = fc-51 [package=THT]
  M4 = fc-51 [package=THT]
  Part1 = Arduino Nano (Rev3.0)
  Part2 = RFID-RC522-v2
  U1 = NodeMCU V3.0
  SERVO1 = Tower Pro SG90 servo [part_number=101246]
  Part3 = LCD1602-I2C
  Power_plug1 = Power plug
  J1 = Piezo Speaker

nets:
  N1: M1.pin1, Part1.A0
  GND: M1.pin2, M2.pin2, M4.pin2, Part1.GND, Part2.GND, U1.GND#16, SERVO1.GND, Part3.GND, Power_plug1.GND
  N2: M1.pin3, M2.pin3, M3.pin3, M4.pin3, Part1.5V
  N3: M2.pin1, Part1.A1
  N4: M3.pin1, Part1.A2
  N5: M4.pin1, Part1.A3
  N6: Part1.D2, U1.D5
  N7: Part1.D3, U1.D6
  N8: Part1.D9, Part2.RST
  N9: Part1.D10, Part2.SDA
  N10: Part1.D11/MOSI, Part2.MOSI
  N11: Part1.D12/MISO, Part2.MISO
  VIN: Part1.VIN, U1.Vin, SERVO1.+5V, Part3.VCC, Power_plug1.VCC
  3V3: Part1.3V3, Part2.3.3V
  N12: Part1.D13/SCK, Part2.SCK
  N13: U1.D1, Part3.SDA
  N14: U1.D2, Part3.SCL
  N15: U1.D3, J1.pin2
  N16: U1.D7, SERVO1.Signal
  N17: U1.GND#41, J1.pin1

custom parts:
  RFID-RC522-v2: A simple China made RFID-RC522 Reader; do check the pin labels, as this is a MFRC522 based clone.
  NodeMCU V3.0: ESP8266 based NodeMCU
  Tower Pro SG90 servo: Original file by John De Cristofaro http://www.adafruit.com/products/1449 Adafruit Feedback Servo (Small) Edited by: e-radionica.com 28/9/2015
  LCD1602-I2C: A standard character display, usually with 2x16 characters. Comes in many colors with LCM1602 IIC attached.
