# Fritzing sketch Untitled Sketch (saved by Fritzing 0.9.3b)

parts:
  U1 = NodeMCU V3.0
  SERVO1 = Tower Pro SG90 servo [part_number=101246]
  J1 = Buzzer
  Part1 = LCD1602-I2C
  S1 = Round Pushbutton
  R1 = Resistor [tolerance=±5% resistance=220 package="0402 [SMD]"]
  IC1 = Voltage Regulator [package=to-220-alt]
  C1 = Capacitor Polarized [package=panasonic_c]
  C2 = Capacitor Polarized [package=panasonic_c]
  VCC1 = Battery block 9V

nets:
  N1: U1.D1, Part1.SDA
  N2: U1.D2, Part1.SCL
  N3: U1.D3, J1.pin2
  N4: U1.D5, S1.leg1, R1.Pin_0
  N5: U1.D6, SERVO1.Signal
  N6: U1.VU, Part1.VCC
  N7: U1.GND#41, Part1.GND
  N8: SERVO1.+5V, S1.leg0
  N9: SERVO1.GND, R1.Pin_1
  N10: IC1.GND, C1.+, VCC1.+
  N11: IC1.IN, C1.-, C2.-, VCC1.-
  N12: IC1.OUT, C2.+

custom parts:
  NodeMCU V3.0: ESP8266 based NodeMCU
  Tower Pro SG90 servo: Original file by John De Cristofaro http://www.adafruit.com/products/1449 Adafruit Feedback Servo (Small) Edited by: e-radionica.com 28/9/2015
  Buzzer: Fixed frequency buzzer
  LCD1602-I2C: A standard character display, usually with 2x16 characters. Comes in many colors with LCM1602 IIC attached.
