# Fritzing sketch Untitled Sketch (saved by Fritzing 0.9.3b)

parts:
  LCD2004-I2C1 = LCD2004-I2C
  U1 = NodeMCU V3.0
  R1 = Resistor [tolerance=±5% resistance=220 package=THT]
  R2 = Resistor [tolerance=±5% resistance=220 package=THT]
  J1 = Piezo Speaker
  S1 = Momentary Switch [package=ksa_sealed_tac_switch]
  S2 = Momentary Switch [package=ksa_sealed_tac_switch]
  IC1 = Voltage Regulator [package=to-220-alt]
  C1 = Electrolytic Capacitor [capacitance=10μF package="0605 [SMD, electrolytic]"]
  BAT1 = BC9VPC [package=bc9vpc]
  C2 = Electrolytic Capacitor [capacitance=10μF package="0605 [SMD, electrolytic]"]

nets:
  N1: LCD2004-I2C1.GND, U1.GND#41, R1.Pin_1, R2.Pin_0, J1.pin1
  N2: LCD2004-I2C1.VCC, U1.VU, S1.1, S2.1
  N3: LCD2004-I2C1.SDA, U1.D1
  N4: LCD2004-I2C1.SCL, U1.D2
  N5: U1.GND#6, U1.GND#16, IC1.IN, C1.-, BAT1.V-
  N6: U1.D5, J1.pin2
  N7: U1.D6, S2.3
  N8: U1.D7, S1.3
  VIN: U1.Vin, IC1.GND, C2.+
  N9: IC1.OUT, C1.+, BAT1.V+

custom parts:
  LCD2004-I2C: A standard character display with 4x20 characters. Comes in many colors with LCM2004 IIC attached.
  NodeMCU V3.0: ESP8266 based NodeMCU
