# Fritzing sketch smart home (saved by Fritzing 0.9.3b)

parts:
  8_Channel_Relay1 = 8 Channel Power Relay
  U1 = NodeMCU V3.0
  LED1 = LEDs [package=led10mm]
  LED2 = LEDs [package=led10mm]
  LED3 = LEDs [package=led10mm]
  LED4 = LEDs [package=led10mm]
  LED5 = LEDs [package=led10mm]
  Part3 = LilyPad Coin Cell Battery Holder
  Part4 = LilyPad Coin Cell Battery Holder
  Power_plug1 = Power plug
  Power_plug2 = Power plug  # not connected

nets:
  GND: 8_Channel_Relay1.GND, U1.GND
  N1: 8_Channel_Relay1.IN1, U1.D0
  N2: 8_Channel_Relay1.IN2, U1.D1
  N3: 8_Channel_Relay1.IN3, U1.D2
  N4: 8_Channel_Relay1.IN4, U1.D3
  N5: 8_Channel_Relay1.IN5, U1.D4
  N6: 8_Channel_Relay1.IN6, U1.D5
  N7: 8_Channel_Relay1.IN7, U1.D6
  N8: 8_Channel_Relay1.IN8, U1.D7
  N9: 8_Channel_Relay1.VCC, U1.VU
  N10: 8_Channel_Relay1.COM#22, 8_Channel_Relay1.COM#25, 8_Channel_Relay1.COM#28
  N11: 8_Channel_Relay1.NO#23, LED1.A
  N12: 8_Channel_Relay1.NO#26, LED2.C
  N13: 8_Channel_Relay1.NO#29, LED3.C
  N14: 8_Channel_Relay1.NO#32, LED4.C
  N15: 8_Channel_Relay1.NO#35, LED5.A
  N16: 8_Channel_Relay1.NO#38, 8_Channel_Relay1.NO#41, LED1.C, LED2.A, LED3.A, LED4.A, LED5.C, Part3.+, Part4.+
  VIN: U1.Vin, Power_plug1.VCC

notes:
  [ 5Vdc supply ]
  ~ [ 220 - 250 Vac]
  [Socket outlet]

custom parts:
  8 Channel Power Relay: An 8 channel power relay. The module operates at 5V.
  NodeMCU V3.0: ESP8266 based NodeMCU
  LEDs: LEDs Standard schematic elements and footprints for 5mm, 3mm, 1206, and 0603 sized LEDs. 5mm - Spark Fun Electronics SKU : COM-00529 (and others)
