# Fritzing sketch Untitled Sketch (saved by Fritzing 0.9.3b)

parts:
  VALVE1 = Plastic Solenoid Valve
  Part1 = Arduino Uno (Rev3) - ICSP
  GSM_SIM_GPSR_SMS_SIM900_SIM1 = SIM800L [package=THT]
  YF-S201_Flow_Meter1 = YF-S201 Water Flow Meter
  kEYPAD_MATRICIAL_1 = KEYPAD 4x3
  U1 = LM2596 step down module
  LED1 = RGB LED (com. cathode, rbg) [package="5 mm [THT]"]
  JACK1 = 2.1mm Barrel Jack with Terminal Block
  Part2 = Solid State High Level Relay Module [package=relay]
  Part3 = LCD1602-I2C

nets:
  N1: VALVE1.no_name_yet#1, Part2.A1
  GND: VALVE1.no_name_yet#2, Part1.GND, GSM_SIM_GPSR_SMS_SIM900_SIM1.GND, YF-S201_Flow_Meter1.GND, U1.IN-, U1.OUT-, LED1.common_cathode, JACK1.POS, Part2.DC-, Part3.GND
  N2: Part1.A0, LED1.green_anode
  N3: Part1.A1, LED1.blue_anode
  N4: Part1.A2, LED1.red_anode
  N5: Part1.A4/SDA, Part3.SDA
  N6: Part1.A5/SCL, Part3.SCL
  N7: Part1.D8, kEYPAD_MATRICIAL_1.arrow1
  N8: Part1.D9_PWM, kEYPAD_MATRICIAL_1.col1
  N9: Part1.D10_PWM/SS, GSM_SIM_GPSR_SMS_SIM900_SIM1.SIM_RXD
  N10: Part1.D11_PWM/MOSI, GSM_SIM_GPSR_SMS_SIM900_SIM1.SIM_TXD
  N11: Part1.D12/MISO, Part2.CH1
  N12: Part1.D2, YF-S201_Flow_Meter1.SIG
  N13: Part1.D3_PWM, kEYPAD_MATRICIAL_1.arrow4
  N14: Part1.D4, kEYPAD_MATRICIAL_1.arrow3
  N15: Part1.D5_PWM, kEYPAD_MATRICIAL_1.col3
  N16: Part1.D6_PWM, kEYPAD_MATRICIAL_1.arrow2
  N17: Part1.D7, kEYPAD_MATRICIAL_1.col2
  VCC: Part1.5V, YF-S201_Flow_Meter1.VCC, Part2.DC+, Part3.VCC
  VIN: Part1.VIN, GSM_SIM_GPSR_SMS_SIM900_SIM1.5V, U1.OUT+
  N18: U1.IN+, JACK1.NEG, Part2.B1

custom parts:
  YF-S201 Water Flow Meter: The YF-S201 Flow Meter. The input voltage is 5V to 24V (DC).
  KEYPAD 4x3: KEYPAD matricial de 12 botones, 4 filas x 3 columnas
  LM2596 step down module: LM2596 DC-DC step down power supply module 3 A.
  Solid State High Level Relay Module: 5V Omron solid state relay 240V 2A output with resistance fuse.
  LCD1602-I2C: A standard character display, usually with 2x16 characters. Comes in many colors with LCM1602 IIC attached.
